# Fritzing sketch led_control_esp (saved by Fritzing 0.9.9b)
breadboards: 1

parts:
  Q1 = PNP-Transistor [package="TO92 [THT]"]
  LED1 = RGB LED (com. anode, rbg) [package="5 mm [THT]"]
  Power_plug1 = Power plug
  U1 = ESP8266 NodeMCU LoLin module
  Q2 = PNP-Transistor [package="TO92 [THT]"]
  Q3 = PNP-Transistor [package="TO92 [THT]"]
  KY-1 = Keyes Relay [package=THT]
  Power_plug2 = Power plug

nets:
  GND: Q1.E, U1.GND, Q2.E, Q3.E, Power_plug2.GND
  N1: Q1.B, LED1.red_cathode
  N2: Q1.C, U1.D7
  N3: LED1.common_anode, KY-1.power, KY-1.NO
  N4: LED1.blue_cathode, Q2.B
  N5: LED1.green_cathode, Q3.B
  N6: Power_plug1.GND, KY-1.ground
  N7: Power_plug1.VCC, KY-1.C
  N8: U1.D0, KY-1.signal
  N9: U1.D5, Q3.C
  N10: U1.D6, Q2.C
  VIN: U1.Vin, Power_plug2.VCC

notes:
  +12V Power Supply
  +5V Power Supply

custom parts:
  ESP8266 NodeMCU LoLin module: ESP8266 based NodeMCU
  Keyes Relay: The Keyes 5V relay module is suitable for SCM development, home appliance control. It uses a 5V~12V TIL control signal which can control DC / AC signal.
